// Logisim project simplest_scheme.circ as structural Verilog: 1 circuit, main circuit main
module main (
  input  [5:0] in_1,
  input  [15:0] bus_0
);

  wire and_2_out, button_1_out, cdm16_1_iack, Clock, comparator_1_eq, comparator_2_eq, mem, memMux,
       not_1_out, rd, rom_1_p4, s_r_ff_1_q, word;
  wire [5:0] adder_1_out;
  wire [6:0] cdm16_1_data_out, keyboard_1_data;
  wire [8:0] cdm16_1_data_out_2;
  wire [15:0] addr, cdm16_1_pc, cdm16_1_ps, cdm16_1_r0, cdm16_1_r2, cdm16_1_r6, cdm16_1_sp,
       controlled_buffer_2_out, data, kbdMemIn, multiplexer_1_out;

  Button button_1 (.out(button_1_out));
  Clock clock_1 (.out(Clock));
  S_R_Flip_Flop s_r_ff_1 (
    .S(button_1_out), .clk(Clock), .R(cdm16_1_iack), .Q(s_r_ff_1_q));  // open: Qn, preset, reset, en
  Adder #(.width(6)) adder_1 (.a(in_1), .b(6'b000101), .out(adder_1_out));  // open: cin, cout
  // Debugger debugger_1: pin names not known
  // Probe on cdm16_1_r0
  // Probe on cdm16_1_r6
  // Probe on cdm16_1_r2
  cdm16 cdm16_1 (
    .IRQ(s_r_ff_1_q), .int_vec(adder_1_out), .mem(mem), .rd_wr_prime(rd), .address(addr), .word(word),
    .R0(cdm16_1_r0), .R2(cdm16_1_r2), .R6(cdm16_1_r6), .PC(cdm16_1_pc), .PS(cdm16_1_ps), .SP(cdm16_1_sp),
    .data_out({cdm16_1_data_out_2, cdm16_1_data_out}), .data_in(multiplexer_1_out), .clock(Clock),
    .IAck(cdm16_1_iack));  // open: EXC, exc_vec, hold, data_ins_prime, R1, R3, R4, R5, FP, status, fetch
  // Probe on cdm16_1_pc
  // Probe on cdm16_1_sp
  // Probe on cdm16_1_ps
  Comparator #(.width(16)) comparator_1 (.a(addr), .b(16'hbeef), .eq(comparator_1_eq));  // open: gt, lt
  Multiplexer #(.width(16), .enable("false")) multiplexer_1 (
    .in0(controlled_buffer_2_out), .in1(kbdMemIn), .out(multiplexer_1_out), .sel(memMux));
  Comparator #(.width(16)) comparator_2 (.a(addr), .b(16'hdead), .eq(comparator_2_eq));  // open: gt, lt
  and and_1 (memMux, rd, mem, ~word, comparator_1_eq);  // AND_Gate
  and and_2 (and_2_out, ~rd, mem, ~word, comparator_2_eq);  // AND_Gate
  TTY tty_1 (.data(cdm16_1_data_out), .clk(and_2_out));  // open: we, clr
  Keyboard #(.trigger("falling")) keyboard_1 (.clk(memMux), .data(keyboard_1_data));  // open: re, clr, avail
  not not_1 (not_1_out, rd);
  assign data = not_1_out ? {cdm16_1_data_out_2, cdm16_1_data_out} : 16'bz;  // Controlled_Buffer controlled_buffer_1
  assign controlled_buffer_2_out = rd ? data : 16'bz;  // Controlled_Buffer controlled_buffer_2
  assign kbdMemIn = {{9{1'b0}}, keyboard_1_data};  // Bit_Extender bit_extender_1
  // ROM rom_1: pin names not known; wires that end beside it: bus_0, 1'b1, 1'b1, rom_1_p4
  // RAM ram_1: pin names not known; wires that end beside it: addr, word, mem, Clock, rd, data
  // Probe on rom_1_p4
endmodule
