// Logisim project test.circ as structural Verilog: 1 circuit, main circuit main
module main (
  input  [15:0] in_1,
  input  [15:0] in_2,
  input  [2:0] op_type,
  input  [2:0] func,
  input  Cin,
  input  [15:0] A,
  input  [15:0] B,
  input  [2:0] shift_count
);

  wire adder16_1_p3, alu_epty_1_p7, alu_epty_1_p8, test_1_p1, test_1_p2, test_2_p1, test_2_p2;

  // test test_1: pin names not known; wires that end beside it: test_1_p1, test_1_p2
  // test test_2: pin names not known; wires that end beside it: test_2_p1, test_2_p2
  Button button_1 (.out(test_1_p1));
  // Probe on test_1_p2
  Button button_2 (.out(test_2_p1));
  // Probe on test_2_p2
  // ALU_epty alu_epty_1: pin names not known; wires that end beside it: Cin, op_type, func, shift_count, A, B, alu_epty_1_p7, alu_epty_1_p8
  // Probe on in_2
  // adder16 adder16_1: pin names not known; wires that end beside it: in_1, in_2, adder16_1_p3, adder16_1_p3, adder16_1_p3
  // Probe on adder16_1_p3
  // Probe on in_1
  // Probe on A
  // Probe on A
  // Probe on B
  // Probe on B
  // Probe on alu_epty_1_p7
  // Probe on alu_epty_1_p8
  // Probe on alu_epty_1_p8
  // Probe on alu_epty_1_p8
  // Probe on adder16_1_p3
endmodule
